# Fritzing sketch conexion flame y bmp (saved by Fritzing 0.9.10b)
breadboards: 1

parts:
  Componente1 = Arduino Uno (Rev3)
  Componente2 = Adafruit BMP388 - Barometric Pressure and Altimeter [part_number="Adafruit #3966"]
  Mod1 = KY-026 Flame Sensor Module [package="Breakout board"]

nets:
  N1: Componente1.A4/SDA, Componente2.SDO/ADR, Componente2.SDI/SDA
  N2: Componente1.A5/SCL, Componente2.SCK/SCL
  3V3: Componente1.3V3, Componente2.3.3V, Mod1.+
  GND: Componente1.GND, Componente2.GND, Mod1.G

custom parts:
  KY-026 Flame Sensor Module: KY-026 Flame Sensor Module reacts in the presence of fire.
