# Fritzing sketch conexion_sensores-lcd (saved by Fritzing 0.9.3b)
breadboards: 1

parts:
  부품1 = FC-28 Soil Hygrometer Module - Probe
  부품2 = FC-28 Soil Hygrometer Module
  부품3 = Arduino Uno (Rev3)
  DHT11 = DHT11 Humitidy and Temperature Sensor
  LCM1602_IIC1 = LCM1602 IIC [part_number="LCM1602 IIC" chip_label="LCM1602 IIC" package="DIP (Dual Inline) [THT]"]
  U1 = LCD-16X2 [package=lcd-16x2]

nets:
  N1: 부품1.POS, 부품2.POS
  N2: 부품1.NEG, 부품2.NEG
  VCC: 부품2.VCC, 부품3.5V, DHT11.VDD, LCM1602_IIC1.VCC
  GND: 부품2.GND, 부품3.GND, DHT11.GND, LCM1602_IIC1.GND
  N3: 부품2.AO, 부품3.A3
  N4: 부품3.A4/SDA, LCM1602_IIC1.SDA
  N5: 부품3.A5/SCL, LCM1602_IIC1.SCL
  N6: 부품3.D9_PWM, DHT11.DATA
  VSS: LCM1602_IIC1.VSS, U1.VSS
  VDD: LCM1602_IIC1.VDD, U1.VDD
  N7: LCM1602_IIC1.V0, U1.VO
  N8: LCM1602_IIC1.RS, U1.RS
  N9: LCM1602_IIC1.RW, U1.R_W
  N10: LCM1602_IIC1.E, U1.E
  N11: LCM1602_IIC1.D0, U1.DB0
  N12: LCM1602_IIC1.D1, U1.DB1
  N13: LCM1602_IIC1.D2, U1.DB2
  N14: LCM1602_IIC1.D3, U1.DB3
  N15: LCM1602_IIC1.D4, U1.DB4
  N16: LCM1602_IIC1.D5, U1.DB5
  N17: LCM1602_IIC1.D6, U1.DB6
  N18: LCM1602_IIC1.D7, U1.DB7
  N19: LCM1602_IIC1.A, U1.A
  N20: LCM1602_IIC1.K, U1.K
  N21: LCM1602_IIC1.LED_A, LCM1602_IIC1.LED_B

custom parts:
  FC-28 Soil Hygrometer Module - Probe: The FC-28 is a soil hygrometer module that uses the Texas Instruments LM393 comparator chip to provide an analog measurement of soil humidity.
  FC-28 Soil Hygrometer Module: The FC-28 is a soil hygrometer module that uses the Texas Instruments LM393 comparator chip to provide an analog measurement of soil humidity. The digital output is high when soil moisture is over a certain threshold, as determined by adjusting the potentiometer.
  DHT11 Humitidy and Temperature Sensor: DHT11 Humidity and Temperature Sensor
  LCM1602 IIC: I2C-Module to use a 1602 or 2004 LCD on with the wire.h libory Serial LCD Modul
